// Logisim project computer.circ as structural Verilog: 20 circuits, main circuit main
module main (
  input  [15:0] in_1,
  input  in_2
);

  wire clock_1_out;

  Clock clock_1 (.out(clock_1_out));
  Computer computer_1 (.IRQ(in_1), .Reset(in_2), .CLK(clock_1_out));
endmodule

module Adder_16 (
  input  Cin,
  input  [15:0] A,
  input  [15:0] B,
  output [15:0] S,
  output Cout
);

  wire adder_1_cout, adder_2_cout, adder_3_cout, adder_4_cout, adder_5_cout, adder_6_cout, adder_7_cout,
       multiplexer_1_out, multiplexer_2_out;
  wire [3:0] adder_2_out, adder_3_out, adder_4_out, adder_5_out, adder_6_out, adder_7_out;

  Adder #(.width(4)) adder_1 (.a(A[3:0]), .b(B[3:0]), .out(S[3:0]), .cin(Cin), .cout(adder_1_cout));
  Adder #(.width(4)) adder_2 (.a(A[7:4]), .b(B[7:4]), .out(adder_2_out), .cin(1'b1), .cout(adder_2_cout));
  Multiplexer multiplexer_1 (.in0(adder_5_cout), .in1(adder_2_cout), .out(multiplexer_1_out), .sel(adder_1_cout));
  Adder #(.width(4)) adder_3 (.a(A[11:8]), .b(B[11:8]), .out(adder_3_out), .cin(1'b1), .cout(adder_3_cout));
  Multiplexer multiplexer_2 (.in0(adder_6_cout), .in1(adder_3_cout), .out(multiplexer_2_out), .sel(multiplexer_1_out));
  Adder #(.width(4)) adder_4 (.a(A[15:12]), .b(B[15:12]), .out(adder_4_out), .cin(1'b1), .cout(adder_4_cout));
  Multiplexer multiplexer_3 (.in0(adder_7_cout), .in1(adder_4_cout), .out(Cout), .sel(multiplexer_2_out));
  Adder #(.width(4)) adder_5 (.a(A[7:4]), .b(B[7:4]), .out(adder_5_out), .cin(1'b0), .cout(adder_5_cout));
  Adder #(.width(4)) adder_6 (.a(A[11:8]), .b(B[11:8]), .out(adder_6_out), .cin(1'b0), .cout(adder_6_cout));
  Adder #(.width(4)) adder_7 (.a(A[15:12]), .b(B[15:12]), .out(adder_7_out), .cin(1'b0), .cout(adder_7_cout));
  Multiplexer #(.width(4)) multiplexer_4 (.in0(adder_5_out), .in1(adder_2_out), .out(S[7:4]), .sel(adder_1_cout));
  Multiplexer #(.width(4)) multiplexer_5 (.in0(adder_6_out), .in1(adder_3_out), .out(S[11:8]), .sel(multiplexer_1_out));
  Multiplexer #(.width(4)) multiplexer_6 (
    .in0(adder_7_out), .in1(adder_4_out), .out(S[15:12]), .sel(multiplexer_2_out));
endmodule

module Arithmetic (
  input  [15:0] A,
  input  [15:0] B,
  input  [2:0] arith_fn,
  input  [1:0] cmp_fn,
  output [15:0] S,
  output [15:0] Y
);

  wire bitselector_1_out, bitselector_2_out, bitselector_3_out, nand_1_out, nand_2_out, nand_3_out,
       nand_4_out, nand_5_out, nand_6_out, negative, not_1_out, not_2_out, not_3_out, not_4_out, not_5_out,
       not_6_out, not_7_out, overflow, XA, XB, zero;
  wire [15:0] complementer_16_1_output_word, complementer_16_2_output_word;

  Complementer_16 complementer_16_1 (.input_word(A), .negate(arith_fn[1]), .output_word(complementer_16_1_output_word));
  Complementer_16 complementer_16_2 (.input_word(B), .negate(arith_fn[2]), .output_word(complementer_16_2_output_word));
  buf buffer_1 (XB, bitselector_1_out);
  BitSelector #(.width(16)) bitselector_1 (.in(complementer_16_2_output_word), .out(bitselector_1_out), .sel(4'b1111));
  buf buffer_2 (XA, bitselector_2_out);
  BitSelector #(.width(16)) bitselector_2 (.in(complementer_16_1_output_word), .out(bitselector_2_out), .sel(4'b1111));
  Adder_16 adder_16_1 (
    .Cin(arith_fn[0]), .A(complementer_16_1_output_word), .B(complementer_16_2_output_word), .S(S));  // open: Cout
  not not_1 (not_1_out, negative);
  not not_2 (not_2_out, XA);
  not not_3 (not_3_out, XB);
  not not_4 (not_4_out, overflow);
  not not_5 (not_5_out, negative);
  not not_6 (not_6_out, overflow);
  not not_7 (not_7_out, negative);
  nand nand_1 (nand_1_out, XA, XB, not_1_out);
  nand nand_2 (nand_2_out, not_2_out, not_3_out, negative);
  nand nand_3 (nand_3_out, cmp_fn[0], zero, not_4_out);
  nand nand_4 (nand_4_out, cmp_fn[0], zero, not_5_out);
  nand nand_5 (nand_5_out, cmp_fn[1], negative, not_6_out);
  nand nand_6 (nand_6_out, cmp_fn[1], overflow, not_7_out);
  BitSelector #(.width(16)) bitselector_3 (.in(S), .out(bitselector_3_out), .sel(4'b1111));
  nand nand_7 (overflow, nand_1_out, nand_2_out);
  nand nand_8 (Y[0], nand_3_out, nand_4_out, nand_5_out, nand_6_out);
  buf buffer_3 (negative, bitselector_3_out);
  Compare0_16 compare0_16_1 (.A(S), .Z(zero));

  assign Y[15:1] = {15{1'b0}};

  // Other names for the same wires on the sheet: equal_fn = cmp_fn[0]; less_fn = cmp_fn[1]

  // Notes on the sheet:
  //   arith_fn :
  //   000 : A+B
  //   001 : A+B+1
  //   011 : -A+B (redundant #2)
  //   101 : A-B (redundant #2)
  //   110 : -A-B-2
  //   111 : -A-B-1
  //   cmp_fn :
  //   00 : always false
  //   01 : equal
  //   10 : less than
  //   11 : less or equal
  //   010 : -A+B-1 (rendundant #1)
  //   100 : A-B-1 (rendundant #1)
endmodule

module Complementer_16 (
  input  [15:0] input_word,
  input  negate,
  output [15:0] output_word
);

  xor xor_1 (output_word[15], input_word[15], negate);
  xor xor_2 (output_word[14], input_word[14], negate);
  xor xor_3 (output_word[13], input_word[13], negate);
  xor xor_4 (output_word[12], input_word[12], negate);
  xor xor_5 (output_word[11], input_word[11], negate);
  xor xor_6 (output_word[10], input_word[10], negate);
  xor xor_7 (output_word[9], input_word[9], negate);
  xor xor_8 (output_word[8], input_word[8], negate);
  xor xor_9 (output_word[7], input_word[7], negate);
  xor xor_10 (output_word[6], input_word[6], negate);
  xor xor_11 (output_word[5], input_word[5], negate);
  xor xor_12 (output_word[4], input_word[4], negate);
  xor xor_13 (output_word[3], input_word[3], negate);
  xor xor_14 (output_word[2], input_word[2], negate);
  xor xor_15 (output_word[1], input_word[1], negate);
  xor xor_16 (output_word[0], input_word[0], negate);
endmodule

module Compare0_16 (
  input  [15:0] A,
  output Z
);

  wire nor_1_out, nor_2_out, nor_3_out, nor_4_out;

  nor nor_1 (nor_1_out, A[0], A[1], A[2], A[3]);
  nor nor_2 (nor_2_out, A[4], A[5], A[6], A[7]);
  nor nor_3 (nor_3_out, A[8], A[9], A[10], A[11]);
  nor nor_4 (nor_4_out, A[12], A[13], A[14], A[15]);
  and and_1 (Z, nor_1_out, nor_2_out, nor_3_out, nor_4_out);
endmodule

module Bitwise_16 (
  input  [3:0] bool_fn,
  input  [15:0] A,
  input  [15:0] B,
  input  bsex,
  output [15:0] Y
);

  wire [15:0] fullsex_16_1_y, multiplexer_1_out;

  Multiplexer #(.width(16)) multiplexer_1 (.in0(B), .in1(fullsex_16_1_y), .out(multiplexer_1_out), .sel(bsex));
  FullSex_16 fullsex_16_1 (.A(B), .Y(fullsex_16_1_y));
  Multiplexer #(.select(2)) multiplexer_2 (
    .in0(bool_fn[0]), .in1(bool_fn[1]), .in2(bool_fn[2]), .in3(bool_fn[3]), .out(Y[0]),
    .sel({multiplexer_1_out[0], A[0]}));
  Multiplexer #(.select(2)) multiplexer_3 (
    .in0(bool_fn[0]), .in1(bool_fn[1]), .in2(bool_fn[2]), .in3(bool_fn[3]), .out(Y[1]),
    .sel({multiplexer_1_out[1], A[1]}));
  Multiplexer #(.select(2)) multiplexer_4 (
    .in0(bool_fn[0]), .in1(bool_fn[1]), .in2(bool_fn[2]), .in3(bool_fn[3]), .out(Y[2]),
    .sel({multiplexer_1_out[2], A[2]}));
  Multiplexer #(.select(2)) multiplexer_5 (
    .in0(bool_fn[0]), .in1(bool_fn[1]), .in2(bool_fn[2]), .in3(bool_fn[3]), .out(Y[3]),
    .sel({multiplexer_1_out[3], A[3]}));
  Multiplexer #(.select(2)) multiplexer_6 (
    .in0(bool_fn[0]), .in1(bool_fn[1]), .in2(bool_fn[2]), .in3(bool_fn[3]), .out(Y[4]),
    .sel({multiplexer_1_out[4], A[4]}));
  Multiplexer #(.select(2)) multiplexer_7 (
    .in0(bool_fn[0]), .in1(bool_fn[1]), .in2(bool_fn[2]), .in3(bool_fn[3]), .out(Y[5]),
    .sel({multiplexer_1_out[5], A[5]}));
  Multiplexer #(.select(2)) multiplexer_8 (
    .in0(bool_fn[0]), .in1(bool_fn[1]), .in2(bool_fn[2]), .in3(bool_fn[3]), .out(Y[6]),
    .sel({multiplexer_1_out[6], A[6]}));
  Multiplexer #(.select(2)) multiplexer_9 (
    .in0(bool_fn[0]), .in1(bool_fn[1]), .in2(bool_fn[2]), .in3(bool_fn[3]), .out(Y[7]),
    .sel({multiplexer_1_out[7], A[7]}));
  Multiplexer #(.select(2)) multiplexer_10 (
    .in0(bool_fn[0]), .in1(bool_fn[1]), .in2(bool_fn[2]), .in3(bool_fn[3]), .out(Y[8]),
    .sel({multiplexer_1_out[8], A[8]}));
  Multiplexer #(.select(2)) multiplexer_11 (
    .in0(bool_fn[0]), .in1(bool_fn[1]), .in2(bool_fn[2]), .in3(bool_fn[3]), .out(Y[9]),
    .sel({multiplexer_1_out[9], A[9]}));
  Multiplexer #(.select(2)) multiplexer_12 (
    .in0(bool_fn[0]), .in1(bool_fn[1]), .in2(bool_fn[2]), .in3(bool_fn[3]), .out(Y[10]),
    .sel({multiplexer_1_out[10], A[10]}));
  Multiplexer #(.select(2)) multiplexer_13 (
    .in0(bool_fn[0]), .in1(bool_fn[1]), .in2(bool_fn[2]), .in3(bool_fn[3]), .out(Y[11]),
    .sel({multiplexer_1_out[11], A[11]}));
  Multiplexer #(.select(2)) multiplexer_14 (
    .in0(bool_fn[0]), .in1(bool_fn[1]), .in2(bool_fn[2]), .in3(bool_fn[3]), .out(Y[12]),
    .sel({multiplexer_1_out[12], A[12]}));
  Multiplexer #(.select(2)) multiplexer_15 (
    .in0(bool_fn[0]), .in1(bool_fn[1]), .in2(bool_fn[2]), .in3(bool_fn[3]), .out(Y[13]),
    .sel({multiplexer_1_out[13], A[13]}));
  Multiplexer #(.select(2)) multiplexer_16 (
    .in0(bool_fn[0]), .in1(bool_fn[1]), .in2(bool_fn[2]), .in3(bool_fn[3]), .out(Y[14]),
    .sel({multiplexer_1_out[14], A[14]}));
  Multiplexer #(.select(2)) multiplexer_17 (
    .in0(bool_fn[0]), .in1(bool_fn[1]), .in2(bool_fn[2]), .in3(bool_fn[3]), .out(Y[15]),
    .sel({multiplexer_1_out[15], A[15]}));
endmodule

module Left_Shifter_16 (
  input  [15:0] A,
  input  [3:0] B,
  output [15:0] Y
);

  wire multiplexer_1_out, multiplexer_2_out, multiplexer_3_out, multiplexer_4_out, multiplexer_5_out,
       multiplexer_6_out, multiplexer_7_out, multiplexer_8_out, multiplexer_9_out, multiplexer_10_out,
       multiplexer_11_out, multiplexer_12_out, multiplexer_13_out, multiplexer_14_out, multiplexer_15_out,
       multiplexer_16_out, multiplexer_17_out, multiplexer_18_out, multiplexer_19_out, multiplexer_20_out,
       multiplexer_21_out, multiplexer_22_out, multiplexer_23_out, multiplexer_24_out, multiplexer_25_out,
       multiplexer_26_out, multiplexer_27_out, multiplexer_28_out, multiplexer_29_out, multiplexer_30_out,
       multiplexer_31_out, multiplexer_32_out, multiplexer_33_out, multiplexer_34_out, multiplexer_35_out,
       multiplexer_36_out, multiplexer_37_out, multiplexer_38_out, multiplexer_39_out, multiplexer_40_out,
       multiplexer_41_out, multiplexer_42_out, multiplexer_43_out, multiplexer_44_out, multiplexer_45_out,
       multiplexer_46_out, multiplexer_47_out, multiplexer_48_out;

  Multiplexer multiplexer_1 (.in0(A[0]), .in1(1'b0), .out(multiplexer_1_out), .sel(B[3]));
  Multiplexer multiplexer_2 (.in0(A[1]), .in1(1'b0), .out(multiplexer_2_out), .sel(B[3]));
  Multiplexer multiplexer_3 (.in0(A[2]), .in1(1'b0), .out(multiplexer_3_out), .sel(B[3]));
  Multiplexer multiplexer_4 (.in0(A[3]), .in1(1'b0), .out(multiplexer_4_out), .sel(B[3]));
  Multiplexer multiplexer_5 (.in0(A[4]), .in1(1'b0), .out(multiplexer_5_out), .sel(B[3]));
  Multiplexer multiplexer_6 (.in0(A[5]), .in1(1'b0), .out(multiplexer_6_out), .sel(B[3]));
  Multiplexer multiplexer_7 (.in0(A[6]), .in1(1'b0), .out(multiplexer_7_out), .sel(B[3]));
  Multiplexer multiplexer_8 (.in0(A[7]), .in1(1'b0), .out(multiplexer_8_out), .sel(B[3]));
  Multiplexer multiplexer_9 (.in0(A[8]), .in1(A[0]), .out(multiplexer_9_out), .sel(B[3]));
  Multiplexer multiplexer_10 (.in0(A[9]), .in1(A[1]), .out(multiplexer_10_out), .sel(B[3]));
  Multiplexer multiplexer_11 (.in0(A[10]), .in1(A[2]), .out(multiplexer_11_out), .sel(B[3]));
  Multiplexer multiplexer_12 (.in0(A[11]), .in1(A[3]), .out(multiplexer_12_out), .sel(B[3]));
  Multiplexer multiplexer_13 (.in0(A[12]), .in1(A[4]), .out(multiplexer_13_out), .sel(B[3]));
  Multiplexer multiplexer_14 (.in0(A[13]), .in1(A[5]), .out(multiplexer_14_out), .sel(B[3]));
  Multiplexer multiplexer_15 (.in0(A[14]), .in1(A[6]), .out(multiplexer_15_out), .sel(B[3]));
  Multiplexer multiplexer_16 (.in0(A[15]), .in1(A[7]), .out(multiplexer_16_out), .sel(B[3]));
  Multiplexer multiplexer_17 (.in0(multiplexer_1_out), .in1(1'b0), .out(multiplexer_17_out), .sel(B[2]));
  Multiplexer multiplexer_18 (.in0(multiplexer_2_out), .in1(1'b0), .out(multiplexer_18_out), .sel(B[2]));
  Multiplexer multiplexer_19 (.in0(multiplexer_3_out), .in1(1'b0), .out(multiplexer_19_out), .sel(B[2]));
  Multiplexer multiplexer_20 (.in0(multiplexer_4_out), .in1(1'b0), .out(multiplexer_20_out), .sel(B[2]));
  Multiplexer multiplexer_21 (.in0(multiplexer_5_out), .in1(multiplexer_1_out), .out(multiplexer_21_out), .sel(B[2]));
  Multiplexer multiplexer_22 (.in0(multiplexer_6_out), .in1(multiplexer_2_out), .out(multiplexer_22_out), .sel(B[2]));
  Multiplexer multiplexer_23 (.in0(multiplexer_7_out), .in1(multiplexer_3_out), .out(multiplexer_23_out), .sel(B[2]));
  Multiplexer multiplexer_24 (.in0(multiplexer_8_out), .in1(multiplexer_4_out), .out(multiplexer_24_out), .sel(B[2]));
  Multiplexer multiplexer_25 (.in0(multiplexer_9_out), .in1(multiplexer_5_out), .out(multiplexer_25_out), .sel(B[2]));
  Multiplexer multiplexer_26 (.in0(multiplexer_10_out), .in1(multiplexer_6_out), .out(multiplexer_26_out), .sel(B[2]));
  Multiplexer multiplexer_27 (.in0(multiplexer_11_out), .in1(multiplexer_7_out), .out(multiplexer_27_out), .sel(B[2]));
  Multiplexer multiplexer_28 (.in0(multiplexer_12_out), .in1(multiplexer_8_out), .out(multiplexer_28_out), .sel(B[2]));
  Multiplexer multiplexer_29 (.in0(multiplexer_13_out), .in1(multiplexer_9_out), .out(multiplexer_29_out), .sel(B[2]));
  Multiplexer multiplexer_30 (.in0(multiplexer_14_out), .in1(multiplexer_10_out), .out(multiplexer_30_out), .sel(B[2]));
  Multiplexer multiplexer_31 (.in0(multiplexer_15_out), .in1(multiplexer_11_out), .out(multiplexer_31_out), .sel(B[2]));
  Multiplexer multiplexer_32 (.in0(multiplexer_16_out), .in1(multiplexer_12_out), .out(multiplexer_32_out), .sel(B[2]));
  Multiplexer multiplexer_33 (.in0(multiplexer_17_out), .in1(1'b0), .out(multiplexer_33_out), .sel(B[1]));
  Multiplexer multiplexer_34 (.in0(multiplexer_18_out), .in1(1'b0), .out(multiplexer_34_out), .sel(B[1]));
  Multiplexer multiplexer_35 (.in0(multiplexer_19_out), .in1(multiplexer_17_out), .out(multiplexer_35_out), .sel(B[1]));
  Multiplexer multiplexer_36 (.in0(multiplexer_20_out), .in1(multiplexer_18_out), .out(multiplexer_36_out), .sel(B[1]));
  Multiplexer multiplexer_37 (.in0(multiplexer_21_out), .in1(multiplexer_19_out), .out(multiplexer_37_out), .sel(B[1]));
  Multiplexer multiplexer_38 (.in0(multiplexer_22_out), .in1(multiplexer_20_out), .out(multiplexer_38_out), .sel(B[1]));
  Multiplexer multiplexer_39 (.in0(multiplexer_23_out), .in1(multiplexer_21_out), .out(multiplexer_39_out), .sel(B[1]));
  Multiplexer multiplexer_40 (.in0(multiplexer_24_out), .in1(multiplexer_22_out), .out(multiplexer_40_out), .sel(B[1]));
  Multiplexer multiplexer_41 (.in0(multiplexer_25_out), .in1(multiplexer_23_out), .out(multiplexer_41_out), .sel(B[1]));
  Multiplexer multiplexer_42 (.in0(multiplexer_26_out), .in1(multiplexer_24_out), .out(multiplexer_42_out), .sel(B[1]));
  Multiplexer multiplexer_43 (.in0(multiplexer_27_out), .in1(multiplexer_25_out), .out(multiplexer_43_out), .sel(B[1]));
  Multiplexer multiplexer_44 (.in0(multiplexer_28_out), .in1(multiplexer_26_out), .out(multiplexer_44_out), .sel(B[1]));
  Multiplexer multiplexer_45 (.in0(multiplexer_29_out), .in1(multiplexer_27_out), .out(multiplexer_45_out), .sel(B[1]));
  Multiplexer multiplexer_46 (.in0(multiplexer_30_out), .in1(multiplexer_28_out), .out(multiplexer_46_out), .sel(B[1]));
  Multiplexer multiplexer_47 (.in0(multiplexer_31_out), .in1(multiplexer_29_out), .out(multiplexer_47_out), .sel(B[1]));
  Multiplexer multiplexer_48 (.in0(multiplexer_32_out), .in1(multiplexer_30_out), .out(multiplexer_48_out), .sel(B[1]));
  Multiplexer multiplexer_49 (.in0(multiplexer_33_out), .in1(1'b0), .out(Y[0]), .sel(B[0]));
  Multiplexer multiplexer_50 (.in0(multiplexer_34_out), .in1(multiplexer_33_out), .out(Y[1]), .sel(B[0]));
  Multiplexer multiplexer_51 (.in0(multiplexer_35_out), .in1(multiplexer_34_out), .out(Y[2]), .sel(B[0]));
  Multiplexer multiplexer_52 (.in0(multiplexer_36_out), .in1(multiplexer_35_out), .out(Y[3]), .sel(B[0]));
  Multiplexer multiplexer_53 (.in0(multiplexer_37_out), .in1(multiplexer_36_out), .out(Y[4]), .sel(B[0]));
  Multiplexer multiplexer_54 (.in0(multiplexer_38_out), .in1(multiplexer_37_out), .out(Y[5]), .sel(B[0]));
  Multiplexer multiplexer_55 (.in0(multiplexer_39_out), .in1(multiplexer_38_out), .out(Y[6]), .sel(B[0]));
  Multiplexer multiplexer_56 (.in0(multiplexer_40_out), .in1(multiplexer_39_out), .out(Y[7]), .sel(B[0]));
  Multiplexer multiplexer_57 (.in0(multiplexer_41_out), .in1(multiplexer_40_out), .out(Y[8]), .sel(B[0]));
  Multiplexer multiplexer_58 (.in0(multiplexer_42_out), .in1(multiplexer_41_out), .out(Y[9]), .sel(B[0]));
  Multiplexer multiplexer_59 (.in0(multiplexer_43_out), .in1(multiplexer_42_out), .out(Y[10]), .sel(B[0]));
  Multiplexer multiplexer_60 (.in0(multiplexer_44_out), .in1(multiplexer_43_out), .out(Y[11]), .sel(B[0]));
  Multiplexer multiplexer_61 (.in0(multiplexer_45_out), .in1(multiplexer_44_out), .out(Y[12]), .sel(B[0]));
  Multiplexer multiplexer_62 (.in0(multiplexer_46_out), .in1(multiplexer_45_out), .out(Y[13]), .sel(B[0]));
  Multiplexer multiplexer_63 (.in0(multiplexer_47_out), .in1(multiplexer_46_out), .out(Y[14]), .sel(B[0]));
  Multiplexer multiplexer_64 (.in0(multiplexer_48_out), .in1(multiplexer_47_out), .out(Y[15]), .sel(B[0]));
endmodule

module Right_Shifter_16 (
  input  [15:0] A,
  input  arithmetic,
  input  [3:0] B,
  output [15:0] Y
);

  wire multiplexer_1_out, multiplexer_2_out, multiplexer_3_out, multiplexer_4_out, multiplexer_5_out,
       multiplexer_6_out, multiplexer_7_out, multiplexer_8_out, multiplexer_9_out, multiplexer_10_out,
       multiplexer_11_out, multiplexer_12_out, multiplexer_13_out, multiplexer_14_out, multiplexer_15_out,
       multiplexer_16_out, multiplexer_17_out, multiplexer_18_out, multiplexer_19_out, multiplexer_20_out,
       multiplexer_21_out, multiplexer_22_out, multiplexer_23_out, multiplexer_24_out, multiplexer_25_out,
       multiplexer_26_out, multiplexer_27_out, multiplexer_28_out, multiplexer_29_out, multiplexer_30_out,
       multiplexer_31_out, multiplexer_32_out, multiplexer_33_out, multiplexer_34_out, multiplexer_35_out,
       multiplexer_36_out, multiplexer_37_out, multiplexer_38_out, multiplexer_39_out, multiplexer_40_out,
       multiplexer_41_out, multiplexer_42_out, multiplexer_43_out, multiplexer_44_out, multiplexer_45_out,
       multiplexer_46_out, multiplexer_47_out, multiplexer_48_out, multiplexer_49_out, shift_in;

  buf buffer_1 (shift_in, multiplexer_1_out);
  Multiplexer multiplexer_1 (.in0(1'b0), .in1(A[15]), .out(multiplexer_1_out), .sel(arithmetic));
  Multiplexer multiplexer_2 (.in0(A[0]), .in1(A[8]), .out(multiplexer_2_out), .sel(B[3]));
  Multiplexer multiplexer_3 (.in0(A[1]), .in1(A[9]), .out(multiplexer_3_out), .sel(B[3]));
  Multiplexer multiplexer_4 (.in0(A[2]), .in1(A[10]), .out(multiplexer_4_out), .sel(B[3]));
  Multiplexer multiplexer_5 (.in0(A[3]), .in1(A[11]), .out(multiplexer_5_out), .sel(B[3]));
  Multiplexer multiplexer_6 (.in0(A[4]), .in1(A[12]), .out(multiplexer_6_out), .sel(B[3]));
  Multiplexer multiplexer_7 (.in0(A[5]), .in1(A[13]), .out(multiplexer_7_out), .sel(B[3]));
  Multiplexer multiplexer_8 (.in0(A[6]), .in1(A[14]), .out(multiplexer_8_out), .sel(B[3]));
  Multiplexer multiplexer_9 (.in0(A[7]), .in1(A[15]), .out(multiplexer_9_out), .sel(B[3]));
  Multiplexer multiplexer_10 (.in0(A[8]), .in1(shift_in), .out(multiplexer_10_out), .sel(B[3]));
  Multiplexer multiplexer_11 (.in0(A[9]), .in1(shift_in), .out(multiplexer_11_out), .sel(B[3]));
  Multiplexer multiplexer_12 (.in0(A[10]), .in1(shift_in), .out(multiplexer_12_out), .sel(B[3]));
  Multiplexer multiplexer_13 (.in0(A[11]), .in1(shift_in), .out(multiplexer_13_out), .sel(B[3]));
  Multiplexer multiplexer_14 (.in0(A[12]), .in1(shift_in), .out(multiplexer_14_out), .sel(B[3]));
  Multiplexer multiplexer_15 (.in0(A[13]), .in1(shift_in), .out(multiplexer_15_out), .sel(B[3]));
  Multiplexer multiplexer_16 (.in0(A[14]), .in1(shift_in), .out(multiplexer_16_out), .sel(B[3]));
  Multiplexer multiplexer_17 (.in0(A[15]), .in1(shift_in), .out(multiplexer_17_out), .sel(B[3]));
  Multiplexer multiplexer_18 (.in0(multiplexer_2_out), .in1(multiplexer_6_out), .out(multiplexer_18_out), .sel(B[2]));
  Multiplexer multiplexer_19 (.in0(multiplexer_3_out), .in1(multiplexer_7_out), .out(multiplexer_19_out), .sel(B[2]));
  Multiplexer multiplexer_20 (.in0(multiplexer_4_out), .in1(multiplexer_8_out), .out(multiplexer_20_out), .sel(B[2]));
  Multiplexer multiplexer_21 (.in0(multiplexer_5_out), .in1(multiplexer_9_out), .out(multiplexer_21_out), .sel(B[2]));
  Multiplexer multiplexer_22 (.in0(multiplexer_6_out), .in1(multiplexer_10_out), .out(multiplexer_22_out), .sel(B[2]));
  Multiplexer multiplexer_23 (.in0(multiplexer_7_out), .in1(multiplexer_11_out), .out(multiplexer_23_out), .sel(B[2]));
  Multiplexer multiplexer_24 (.in0(multiplexer_8_out), .in1(multiplexer_12_out), .out(multiplexer_24_out), .sel(B[2]));
  Multiplexer multiplexer_25 (.in0(multiplexer_9_out), .in1(multiplexer_13_out), .out(multiplexer_25_out), .sel(B[2]));
  Multiplexer multiplexer_26 (.in0(multiplexer_10_out), .in1(multiplexer_14_out), .out(multiplexer_26_out), .sel(B[2]));
  Multiplexer multiplexer_27 (.in0(multiplexer_11_out), .in1(multiplexer_15_out), .out(multiplexer_27_out), .sel(B[2]));
  Multiplexer multiplexer_28 (.in0(multiplexer_12_out), .in1(multiplexer_16_out), .out(multiplexer_28_out), .sel(B[2]));
  Multiplexer multiplexer_29 (.in0(multiplexer_13_out), .in1(multiplexer_17_out), .out(multiplexer_29_out), .sel(B[2]));
  Multiplexer multiplexer_30 (.in0(multiplexer_14_out), .in1(shift_in), .out(multiplexer_30_out), .sel(B[2]));
  Multiplexer multiplexer_31 (.in0(multiplexer_15_out), .in1(shift_in), .out(multiplexer_31_out), .sel(B[2]));
  Multiplexer multiplexer_32 (.in0(multiplexer_16_out), .in1(shift_in), .out(multiplexer_32_out), .sel(B[2]));
  Multiplexer multiplexer_33 (.in0(multiplexer_17_out), .in1(shift_in), .out(multiplexer_33_out), .sel(B[2]));
  Multiplexer multiplexer_34 (.in0(multiplexer_18_out), .in1(multiplexer_20_out), .out(multiplexer_34_out), .sel(B[1]));
  Multiplexer multiplexer_35 (.in0(multiplexer_19_out), .in1(multiplexer_21_out), .out(multiplexer_35_out), .sel(B[1]));
  Multiplexer multiplexer_36 (.in0(multiplexer_20_out), .in1(multiplexer_22_out), .out(multiplexer_36_out), .sel(B[1]));
  Multiplexer multiplexer_37 (.in0(multiplexer_21_out), .in1(multiplexer_23_out), .out(multiplexer_37_out), .sel(B[1]));
  Multiplexer multiplexer_38 (.in0(multiplexer_22_out), .in1(multiplexer_24_out), .out(multiplexer_38_out), .sel(B[1]));
  Multiplexer multiplexer_39 (.in0(multiplexer_23_out), .in1(multiplexer_25_out), .out(multiplexer_39_out), .sel(B[1]));
  Multiplexer multiplexer_40 (.in0(multiplexer_24_out), .in1(multiplexer_26_out), .out(multiplexer_40_out), .sel(B[1]));
  Multiplexer multiplexer_41 (.in0(multiplexer_25_out), .in1(multiplexer_27_out), .out(multiplexer_41_out), .sel(B[1]));
  Multiplexer multiplexer_42 (.in0(multiplexer_26_out), .in1(multiplexer_28_out), .out(multiplexer_42_out), .sel(B[1]));
  Multiplexer multiplexer_43 (.in0(multiplexer_27_out), .in1(multiplexer_29_out), .out(multiplexer_43_out), .sel(B[1]));
  Multiplexer multiplexer_44 (.in0(multiplexer_28_out), .in1(multiplexer_30_out), .out(multiplexer_44_out), .sel(B[1]));
  Multiplexer multiplexer_45 (.in0(multiplexer_29_out), .in1(multiplexer_31_out), .out(multiplexer_45_out), .sel(B[1]));
  Multiplexer multiplexer_46 (.in0(multiplexer_30_out), .in1(multiplexer_32_out), .out(multiplexer_46_out), .sel(B[1]));
  Multiplexer multiplexer_47 (.in0(multiplexer_31_out), .in1(multiplexer_33_out), .out(multiplexer_47_out), .sel(B[1]));
  Multiplexer multiplexer_48 (.in0(multiplexer_32_out), .in1(shift_in), .out(multiplexer_48_out), .sel(B[1]));
  Multiplexer multiplexer_49 (.in0(multiplexer_33_out), .in1(shift_in), .out(multiplexer_49_out), .sel(B[1]));
  Multiplexer multiplexer_50 (.in0(multiplexer_34_out), .in1(multiplexer_35_out), .out(Y[0]), .sel(B[0]));
  Multiplexer multiplexer_51 (.in0(multiplexer_35_out), .in1(multiplexer_36_out), .out(Y[1]), .sel(B[0]));
  Multiplexer multiplexer_52 (.in0(multiplexer_36_out), .in1(multiplexer_37_out), .out(Y[2]), .sel(B[0]));
  Multiplexer multiplexer_53 (.in0(multiplexer_37_out), .in1(multiplexer_38_out), .out(Y[3]), .sel(B[0]));
  Multiplexer multiplexer_54 (.in0(multiplexer_38_out), .in1(multiplexer_39_out), .out(Y[4]), .sel(B[0]));
  Multiplexer multiplexer_55 (.in0(multiplexer_39_out), .in1(multiplexer_40_out), .out(Y[5]), .sel(B[0]));
  Multiplexer multiplexer_56 (.in0(multiplexer_40_out), .in1(multiplexer_41_out), .out(Y[6]), .sel(B[0]));
  Multiplexer multiplexer_57 (.in0(multiplexer_41_out), .in1(multiplexer_42_out), .out(Y[7]), .sel(B[0]));
  Multiplexer multiplexer_58 (.in0(multiplexer_42_out), .in1(multiplexer_43_out), .out(Y[8]), .sel(B[0]));
  Multiplexer multiplexer_59 (.in0(multiplexer_43_out), .in1(multiplexer_44_out), .out(Y[9]), .sel(B[0]));
  Multiplexer multiplexer_60 (.in0(multiplexer_44_out), .in1(multiplexer_45_out), .out(Y[10]), .sel(B[0]));
  Multiplexer multiplexer_61 (.in0(multiplexer_45_out), .in1(multiplexer_46_out), .out(Y[11]), .sel(B[0]));
  Multiplexer multiplexer_62 (.in0(multiplexer_46_out), .in1(multiplexer_47_out), .out(Y[12]), .sel(B[0]));
  Multiplexer multiplexer_63 (.in0(multiplexer_47_out), .in1(multiplexer_48_out), .out(Y[13]), .sel(B[0]));
  Multiplexer multiplexer_64 (.in0(multiplexer_48_out), .in1(multiplexer_49_out), .out(Y[14]), .sel(B[0]));
  Multiplexer multiplexer_65 (.in0(multiplexer_49_out), .in1(shift_in), .out(Y[15]), .sel(B[0]));
endmodule

module ALU (
  input  [15:0] A,
  input  [15:0] B,
  input  [6:0] fn,
  output [15:0] Y
);

  wire [3:0] bitselector_1_out, bitselector_2_out;
  wire [15:0] arithmetic_1_s, arithmetic_1_y, bitwise_16_1_y, left_shifter_16_1_y, multiplexer_1_out,
       right_shifter_16_1_y;

  BitSelector #(.group(4), .width(16)) bitselector_1 (.in(B), .out(bitselector_1_out), .sel(2'b00));
  BitSelector #(.group(4), .width(16)) bitselector_2 (.in(B), .out(bitselector_2_out), .sel(2'b00));
  Bitwise_16 bitwise_16_1 (.bool_fn(fn[4:1]), .A(A), .B(B), .bsex(fn[0]), .Y(bitwise_16_1_y));
  Left_Shifter_16 left_shifter_16_1 (.A(A), .B(bitselector_1_out), .Y(left_shifter_16_1_y));
  Right_Shifter_16 right_shifter_16_1 (.A(A), .arithmetic(fn[1]), .B(bitselector_2_out), .Y(right_shifter_16_1_y));
  Arithmetic arithmetic_1 (.A(A), .B(B), .arith_fn(fn[4:2]), .cmp_fn(fn[1:0]), .S(arithmetic_1_s), .Y(arithmetic_1_y));
  Multiplexer #(.width(16)) multiplexer_1 (
    .in0(left_shifter_16_1_y), .in1(right_shifter_16_1_y), .out(multiplexer_1_out), .sel(fn[0]));
  Multiplexer #(.select(2), .width(16)) multiplexer_2 (
    .in0(bitwise_16_1_y), .in1(multiplexer_1_out), .in2(arithmetic_1_s), .in3(arithmetic_1_y), .out(Y),
    .sel(fn[6:5]));

  // Other names for the same wires on the sheet: bsex = fn[0]; bool_fn[3:0] = fn[4:1]
endmodule

module RegisterFile_16x16 (
  input  [15:0] WD15,
  input  WE15,
  input  [3:0] WA,
  input  WE,
  input  [15:0] WD,
  input  CLK,
  input  [3:0] RA1,
  input  [3:0] RA2,
  output [15:0] RD1,
  output [15:0] RD2
);

  wire decoder_1_out0, decoder_1_out1, decoder_1_out2, decoder_1_out3, decoder_1_out4, decoder_1_out5,
       decoder_1_out6, decoder_1_out7, decoder_1_out8, decoder_1_out9, decoder_1_out10, decoder_1_out11,
       decoder_1_out12, decoder_1_out13, decoder_1_out14, decoder_1_out15, or_1_out;
  wire [15:0] multiplexer_3_out, R0_q, R1_q, R2_q, R3_q, R4_q, R5_q, R6_q, R7_q, R8_q, R9_q, R10_q, R11_q,
       R12_q, R13_q, R14_q, R15_q;

  Decoder #(.select(4)) decoder_1 (
    .out0(decoder_1_out0), .out1(decoder_1_out1), .out2(decoder_1_out2), .out3(decoder_1_out3),
    .out4(decoder_1_out4), .out5(decoder_1_out5), .out6(decoder_1_out6), .out7(decoder_1_out7),
    .out8(decoder_1_out8), .out9(decoder_1_out9), .out10(decoder_1_out10), .out11(decoder_1_out11),
    .out12(decoder_1_out12), .out13(decoder_1_out13), .out14(decoder_1_out14), .out15(decoder_1_out15),
    .sel(WA), .en(WE));
  Register #(.width(16)) R0 (.D(WD), .en(decoder_1_out0), .clk(CLK), .Q(R0_q));  // open: clr
  Register #(.width(16)) R1 (.D(WD), .en(decoder_1_out1), .clk(CLK), .Q(R1_q));  // open: clr
  Register #(.width(16)) R2 (.D(WD), .en(decoder_1_out2), .clk(CLK), .Q(R2_q));  // open: clr
  Register #(.width(16)) R3 (.D(WD), .en(decoder_1_out3), .clk(CLK), .Q(R3_q));  // open: clr
  Register #(.width(16)) R4 (.D(WD), .en(decoder_1_out4), .clk(CLK), .Q(R4_q));  // open: clr
  Multiplexer #(.select(4), .width(16)) multiplexer_1 (
    .in0(R0_q), .in1(R1_q), .in2(R2_q), .in3(R3_q), .in4(R4_q), .in5(R5_q), .in6(R6_q), .in7(R7_q),
    .in8(R8_q), .in9(R9_q), .in10(R10_q), .in11(R11_q), .in12(R12_q), .in13(R13_q), .in14(R14_q),
    .in15(R15_q), .out(RD1));  // open: sel
  Register #(.width(16)) R5 (.D(WD), .en(decoder_1_out5), .clk(CLK), .Q(R5_q));  // open: clr
  Register #(.width(16)) R6 (.D(WD), .en(decoder_1_out6), .clk(CLK), .Q(R6_q));  // open: clr
  Register #(.width(16)) R7 (.D(WD), .en(decoder_1_out7), .clk(CLK), .Q(R7_q));  // open: clr
  Register #(.width(16)) R8 (.D(WD), .en(decoder_1_out8), .clk(CLK), .Q(R8_q));  // open: clr
  Multiplexer #(.select(4), .width(16)) multiplexer_2 (
    .in0(R0_q), .in1(R1_q), .in2(R2_q), .in3(R3_q), .in4(R4_q), .in5(R5_q), .in6(R6_q), .in7(R7_q),
    .in8(R8_q), .in9(R9_q), .in10(R10_q), .in11(R11_q), .in12(R12_q), .in13(R13_q), .in14(R14_q),
    .in15(R15_q), .out(RD2));  // open: sel
  Register #(.width(16)) R9 (.D(WD), .en(decoder_1_out9), .clk(CLK), .Q(R9_q));  // open: clr
  Register #(.width(16)) R10 (.D(WD), .en(decoder_1_out10), .clk(CLK), .Q(R10_q));  // open: clr
  Register #(.width(16)) R11 (.D(WD), .en(decoder_1_out11), .clk(CLK), .Q(R11_q));  // open: clr
  Register #(.width(16)) R12 (.D(WD), .en(decoder_1_out12), .clk(CLK), .Q(R12_q));  // open: clr
  Register #(.width(16)) R13 (.D(WD), .en(decoder_1_out13), .clk(CLK), .Q(R13_q));  // open: clr
  Register #(.width(16)) R14 (.D(WD), .en(decoder_1_out14), .clk(CLK), .Q(R14_q));  // open: clr
  or or_1 (or_1_out, WE15, decoder_1_out15);
  Multiplexer #(.width(16)) multiplexer_3 (.in0(WD), .in1(WD15), .out(multiplexer_3_out), .sel(WE15));
  Register #(.width(16)) R15 (.D(multiplexer_3_out), .en(or_1_out), .clk(CLK), .Q(R15_q));  // open: clr
endmodule

module Computer (
  input  [15:0] IRQ,
  input  Reset,
  input  CLK
);

  wire A_SELECT, B_SELECT, bitselector_1_out, compare0_16_1_z, IRQ_CODE_SET, MA_SELECT, MOE, MWE, nand_1_out,
       nand_2_out, not_1_out, NOT_STALL, TIMER_IRQ, TIMER_SET, undriven, WE, WE15;
  wire [1:0] PC_SELECT, WD_SELECT, WD_SELECT_CTRL;
  wire [3:0] EXCEPT_SELECT, IRQ_CODE, multiplexer_1_out, multiplexer_2_out, multiplexer_3_out,
       multiplexer_4_out, RA1, RA2, SAVED_IRQ_CODE, TIMER_DELAY, WA;
  wire [6:0] ALU_FN;
  wire [15:0] CONST, controlled_buffer_2_out, IRQ_BITS_q, IRQ_MASK, multiplexer_5_out, multiplexer_6_out,
       multiplexer_7_out, multiplexer_8_out, multiplexer_9_out, multiplexer_10_out, PC_NEXT, PC_OFFSET, PC_q,
       RA_DATA, ram_1_data, registerfile_16x16_1_rd2, rom_1_data, TICKS, undriven_2;

  Add1_16 add1_16_1 (.S(PC_NEXT), .A(PC_q));
  Multiplexer #(.select(2), .width(4)) multiplexer_1 (
    .in0(4'b0000), .in1(4'b0001), .in2(4'b0010), .in3(4'b0011), .out(multiplexer_1_out),
    .sel(EXCEPT_SELECT[3:2]));
  Multiplexer #(.select(2), .width(4)) multiplexer_2 (
    .in0(4'b0100), .in1(4'b0101), .in2(4'b0110), .in3(4'b0111), .out(multiplexer_2_out),
    .sel(EXCEPT_SELECT[3:2]));
  Multiplexer #(.select(2), .width(4)) multiplexer_3 (
    .in0(4'b1000), .in1(4'b1001), .out(multiplexer_3_out), .sel(EXCEPT_SELECT[3:2]));  // open: in2, in3
  Multiplexer #(.select(2), .width(4)) multiplexer_4 (
    .in0(multiplexer_1_out), .in1(multiplexer_2_out), .in2(multiplexer_3_out), .out(multiplexer_4_out),
    .sel(EXCEPT_SELECT[1:0]));  // open: in3
  Multiplexer #(.select(2), .width(16)) multiplexer_5 (
    .in0(PC_NEXT), .in1(RA_DATA), .in2(PC_OFFSET), .in3({{12{1'b0}}, multiplexer_4_out}),
    .out(multiplexer_5_out), .sel(PC_SELECT));
  not not_1 (not_1_out, NOT_STALL);
  nand nand_1 (nand_1_out, not_1_out, nand_2_out);
  nand nand_2 (nand_2_out, PC_SELECT[0], PC_SELECT[1]);
  Register #(.width(16)) PC (.D(multiplexer_5_out), .en(nand_1_out), .clk(CLK), .Q(PC_q));  // open: clr
  ROM #(.addrWidth(16), .dataWidth(16)) rom_1 (.addr(PC_q), .data(rom_1_data));
  BitSelector #(.width(16)) bitselector_1 (.in(RA_DATA), .out(bitselector_1_out), .sel(4'b1111));
  Compare0_16 compare0_16_1 (.A(RA_DATA), .Z(compare0_16_1_z));
  Register #(.width(4)) u_IRQ_CODE (.D(IRQ_CODE), .en(IRQ_CODE_SET), .clk(CLK), .Q(SAVED_IRQ_CODE));  // open: clr
  Control control_1 (
    .ALU_FN(ALU_FN), .RA1(RA1), .RA2(RA2), .WA(WA), .WE(WE), .CONST(CONST), .B_SELECT(B_SELECT), .MWE(MWE),
    .MOE(MOE), .WD_SELECT(WD_SELECT), .WD_SELECT_CTRL(WD_SELECT_CTRL), .MA_SELECT(MA_SELECT), .WE15(WE15),
    .PC_SELECT(PC_SELECT), .A_SELECT(A_SELECT), .EXCEPT_SELECT(EXCEPT_SELECT), .TIMER_DELAY(TIMER_DELAY),
    .TIMER_SET(TIMER_SET), .IRQ_CODE(IRQ_CODE), .IRQ_CODE_SET(IRQ_CODE_SET), .NOT_STALL(NOT_STALL),
    .IRQ(IRQ), .TIMER_IRQ(TIMER_IRQ), .DEBUG_IRQ(undriven), .IRQ_MASK(IRQ_MASK), .RAZ(compare0_16_1_z),
    .RAN(bitselector_1_out), .Instruction(rom_1_data), .Reset(Reset));
  Timer timer_1 (.CLK(CLK), .DELAY(TIMER_DELAY), .SET(TIMER_SET), .TRIGGER(TIMER_IRQ));
  TickCounter tickcounter_1 (.Reset(Reset), .CLK(CLK), .Ticks(TICKS));
  Register #(.width(16)) u_IRQ_MASK (.D(PC_OFFSET), .en(1'b1), .clk(CLK), .Q(IRQ_MASK));  // open: clr
  Multiplexer #(.width(16)) multiplexer_6 (.in0(PC_NEXT), .in1(RA_DATA), .out(multiplexer_6_out));  // open: sel
  ALU alu_1 (.Y(PC_OFFSET), .A(multiplexer_6_out), .B(multiplexer_7_out), .fn(ALU_FN));
  RegisterFile_16x16 registerfile_16x16_1 (
    .RD1(RA_DATA), .RD2(registerfile_16x16_1_rd2), .RA2(RA2), .WE15(WE15), .WD15(PC_OFFSET), .WE(WE),
    .CLK(CLK), .WD(multiplexer_9_out), .WA(WA), .RA1(RA1));
  Multiplexer #(.width(16)) multiplexer_7 (
    .in0(CONST), .in1(registerfile_16x16_1_rd2), .out(multiplexer_7_out));  // open: sel
  Multiplexer #(.width(16)) multiplexer_8 (.in0(PC_OFFSET), .in1(RA_DATA), .out(multiplexer_8_out));  // open: sel
  RAM #(.addrWidth(16), .dataWidth(16), .databus("bidir")) ram_1 (
    .addr(multiplexer_8_out), .we(MWE), .oe(MOE), .clk(CLK), .data(ram_1_data));
  Multiplexer #(.select(2), .width(16)) multiplexer_9 (
    .in0(PC_NEXT), .in1(PC_OFFSET), .in2(controlled_buffer_2_out), .in3(multiplexer_10_out),
    .out(multiplexer_9_out));  // open: sel
  Register #(.width(16)) IRQ_BITS (.D(IRQ), .en(1'b1), .clk(CLK), .Q(IRQ_BITS_q));  // open: clr
  assign ram_1_data = MWE ? registerfile_16x16_1_rd2 : 16'bz;  // Controlled_Buffer controlled_buffer_1
  assign controlled_buffer_2_out = MOE ? ram_1_data : 16'bz;  // Controlled_Buffer controlled_buffer_2
  Multiplexer #(.select(2), .width(16)) multiplexer_10 (
    .in0(TICKS), .in1(IRQ_BITS_q), .in2({{12{1'b0}}, SAVED_IRQ_CODE}), .in3(undriven_2),
    .out(multiplexer_10_out));  // open: sel
  // NoConnect on undriven_2

  // Notes on the sheet:
  //   contents of rom_1 (hex, n*v repeats v):
  //   0 c032 5974 c802 b418 95e1 62d4 672a 66a2 7d62 ae2f 7aee 4858 5d82 676a 2051 902f 382a 9edb ba6f
  //   c95f cf22 640f 94c4 59e4 e2d5 483f aff3 98a5 2161 7301 e96e eb 6117 9c06 56fa 8a4f b560 a424 2d51
  //   8d59 41fd 4107 2238 e2ba 4f0a 2ff9 4792 950a 2271 c759 8b68 cfcc 1961 1cd 99f4 fa50 a901 64a2 e7aa
  //   ae34 880f 71a5 5327 87c7 b6c8 d731 9748 7f19 46d7 d4a5 bd7d 62dd 3caa 80cf cd31 4ed6 2e9c e0f4 fe2
  //   2eed 1f4f 446a b798 f1c9 a713 c067 6834 62e8 b77f 33fb c877 6858 f367 1364 9f52 c3f5 c7d3 a63e 39f2
  //   6fa8 a75e 13d3 987b 2f8a 33dd de36 afc7 40b5 e9c1 7e13 86d5 dfda 6031 886 459 43b5 3813 e431 6541
  //   1da5 e601 f50d e4fe 8a07 16eb 95f8 85cb e2bc 3031 9d69 de94 3514 7966 567c af4f 48ca ab06 3b3e e093
  //   8cd9 b196 ae42 b935 c03f 6ae5 6b63 a1b 6d0d 6add c730 f65f f359 91d0 9d5d c9ae dc0d 8697 65d4 993
  //   e9b5 4670 d8bd f59d 130c b285 c1bd ef11 78ea c2fa b457 8857 fb34 37d7 b4ea 2020 4f06 dd43 355c 1919
  //   27a2 d0d3 f899 b6af ebfe 6cab 2ed4 feba a07c 4a6a ebe4 6067 af61 1dd9 a3fd 4787 678d 563e af03 c1c5
  //   b7e9 9763 a289 5677 7b15 38e8 342d a31d b2ab 4dd5 3d1 31a 3fc7 ef89 4556 e28e e00c 8bc 8660 8f14
  //   a720 feee 6450 af5e 84ba e5a1 bb7f a112 1b8f 5dc9 d913 436 b54b 9921 5692 ba73 381e d2de 3829 af37
  //   eb4a c980 8688 4a25 9585 af12 2984 77ed 1ac9 a177 2398 9468 82eb 2c6 3e3e 1c82 fc2 250e a612 247b
  //   54b9 4ce4 3206 f0cf b2ea 65bb d09 625f 1033 298a b3c e31b 75b2 6e35 1611 343d 9ecd b546 2af9 8ba7
  //   8d99 a190 695a 4814 6070 3135 8494 b566 d71a 54a0 a7df bfbb e812 f395 e250 7f76 30cc 9bc7 9b7f 7e62
  //   ea6d d785 5344 d02c df78 a292 2329 441e eaab 2e0c 9cc5 53e1 1454 65d9 d773 1923 fd4d a9a9 cfbb aac7
  //   fe91 5440 ce4c 47bc db6 dcf8 f0bb ba65 e9ee 2c52 56a1 492a 6f0f ac35 f7e4 50a3 cc09 6a93 ff16 96f1
  //   2575 80a8 4bb2 6764 4a96 bd35 bd3a 4747 40a1 2446 405c 611d b4b6 3e66 94dd b897 d582 eb0a 1372 8806
  //   a21e a94e b15d 5569 a071 36dc 51c1 f2a5 eabc 5937 7d10 a70c 1dff 7201 93c9 b1ef 720f a57f e538 82d1
  //   f47f 536c 32b d640 d16b 1845 a315 1acd dcce 9f6f 29fb 69c9 44c6 10f8 14fe 2052 d4fa 9e9f 22c9 f85c
  //   5de1 9f2e eca0 f3a8 4bcd 33ee 5ecf 9d9c e9d9 c571 b9c8 11b0 205c d248 dda1 dbf7 2575 def3 235b 8d7e
  //   c517 9141 e03f b003 d4c2 9645 7256 690c 920c 4791 d773 6d16 12d9 b67f ed01 d9c 5646 e17c 8bcf f130
  //   b6c8 2393 62b7 f966 8484 2058 43c1 a799 fb11 7195 32d7 f5a6 ebb9 8fd6 fa87 a2c5 ad32 e648 bd7 cd32
  //   c7fa c4be 90fe cf5b 8b21 2b38 9985 8918 1ce3 e83b 3f93 e37e 9cbb 9a21 5be9 ae03 b68c 29f5 76da 36a7
  //   4785 d888 ea5b d258 e298 f28b ca83 1fb6 934a 6aa2 f8be 2a49 eef6 9733 78b9 d007 966b 110 8ef4 545e
  //   c063 de8b 9e2f e3b9 48f0 87fa 4f9 c622 5ec3 dde3 2d4a 861 db1 698a 803f b5f4 29da 9590 4d46 2ced
  //   1925 8e7 e12d 443e 8508 3a08 dc42 a668 7da9 3617 49ed f37e 2cfe 46dd 6d7a 96d2 d53 3e82 a9db 33df
  //   16a3 4fd4 433d ac65 71a0 48e8 344 e465 aa96 3af 7250 ce d197 df0a 7354 30de 6cfb fb6e 92c5 7951 1f26
  //   e260 5e4f 210c a595 c006 2097 89d5 acd4 ac95 8480 82d4 6846 e7f5 f473 a646 fd1e c7a4 2e7a 9659 7282
  //   4d19 b86 fee0 d500 7cc6 118c 84c ae52 22b2 2b43 5d3c 7b92 74a6 791 53dc cfe4 2285 cc74 193b b8b8
  //   c66a 3776 9b11 6ed5 1f7a 1eff 2627 9546 1e9e d61e 617b 30ae b2d e63e 29a7 171b 1a0b 3981 5a84 163a
  //   e34d 63d3 675d 3417 8bfa 922d a9bf c1b6 acc 854b d4c fee7 2a80 418b 8917 97fc 4a24 f08 1657 a115 6c3
  //   6d7b 45ae f32c 1143 8d39 8983 dd5 4a63 244a e9cc 397b 9cee 69e0 55c1 796b ee6f 1dfd b739 8f15 508e
  //   a527 6b73 8942 8389 ea6d cad2 65b eccd 5390 fde7 e0fe ae33 25d2 df45 a5cb 4a79 33ab 883 2918 ad61
  //   1f97 2a33 5768 e87e 636f 4c66 ebe1 1cbe 399c bc3c d97e eb04 7b65 fc9c adf6 2751 284f a194 14f8 20f4
  //   1c32 3846 777a 8a6d 2635 3e3f d1c1 4478 493a 4346 9ba5 1c06 1fc8 60b 9dd7 f230 c161 2754 ec7d 2f3
  //   d6ce bde1 e010 c23a e532 88e b0ca 72ac fe8c e90b 7bb3 8543 9fe3 1dd a29b 8776 5c6e e280 1e63 e742
  //   36fe cece f4e0 d32f b15 6760 4e0d a08a dab3 e1b8 df02 461b 17da 527 90c0 ed59 4f15 c640 7574 625c
  //   d541 f341 94b2 3b1c cb8 d9a5 a69b 1409 66de 5d0d 12d4 d9f9 c587 7362 ba4 1b00 3dae 676 42b2 86b 50c1
  //   9200 dd09 aee5 75f5 82a6 1a8d ddf0 9f68 139 c2e8 e8fc 49fa e991 42dd 7120 80a5 b7c5 6974 8aba 1760
  //   1643 98b9 14ac abdf dc5f ba16 eb48 c6e1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
  //   <=
  //   =>
  //   <=
  //   =>
endmodule

module FullSex_16 (
  input  [15:0] A,
  output [15:0] Y
);

  wire buffer_1_out;

  buf buffer_1 (buffer_1_out, A[15]);
  buf buffer_2 (Y[3], buffer_1_out);
  buf buffer_3 (Y[7], buffer_1_out);
  buf buffer_4 (Y[11], buffer_1_out);
  buf buffer_5 (Y[15], buffer_1_out);

  assign {Y[14:12], Y[10:8], Y[6:4], Y[2:0]} = {{3{Y[15]}}, {3{Y[11]}}, {3{Y[7]}}, {3{Y[3]}}};
endmodule

module Control (
  input  [15:0] Instruction,
  input  Reset,
  input  [15:0] IRQ,
  input  TIMER_IRQ,
  input  DEBUG_IRQ,
  input  [15:0] IRQ_MASK,
  input  RAZ,
  input  RAN,
  output [6:0] ALU_FN,
  output [3:0] RA1,
  output [3:0] RA2,
  output [3:0] WA,
  output WE,
  output [15:0] CONST,
  output B_SELECT,
  output MWE,
  output MOE,
  output [1:0] WD_SELECT,
  output [1:0] WD_SELECT_CTRL,
  output MA_SELECT,
  output WE15,
  output [1:0] PC_SELECT,
  output A_SELECT,
  output [3:0] EXCEPT_SELECT,
  output [3:0] TIMER_DELAY,
  output TIMER_SET,
  output [3:0] IRQ_CODE,
  output IRQ_CODE_SET,
  output NOT_STALL
);

  wire nand_1_out;
  wire [1:0] RA1_SELECT, RA2_SELECT;
  wire [2:0] CONST_SELECT, WA_SELECT;
  wire [3:3] not_1_out;
  wire [5:0] bitselector_1_out;
  wire [15:0] sex_4_16_1_b, sex_6_16_1_b, sex_6_16_2_b, sex_10_16_1_b;

  ROM #(.addrWidth(6), .dataWidth(37)) rom_1 (
    .addr(bitselector_1_out),
    .data({NOT_STALL, IRQ_CODE_SET, TIMER_SET, EXCEPT_SELECT, PC_SELECT, WE15, MOE, MWE, MA_SELECT, WE, WA_SELECT, WD_SELECT_CTRL, WD_SELECT, ALU_FN, CONST_SELECT, B_SELECT, A_SELECT, RA2_SELECT, RA1_SELECT}));
  BitSelector #(.group(6), .width(16)) bitselector_1 (.in(Instruction), .out(bitselector_1_out), .sel(2'b00));
  nand nand_1 (nand_1_out, Instruction[9], WA_SELECT[2]);
  not not_1 (not_1_out[3], nand_1_out);
  Multiplexer #(.select(2), .width(4)) multiplexer_1 (
    .in0(Instruction[3:0]), .in1({1'b0, Instruction[2:0]}), .in2({Instruction[9], Instruction[2:0]}),
    .in3(4'b1111), .out(RA1), .sel(RA1_SELECT));
  Multiplexer #(.select(2), .width(4)) multiplexer_2 (
    .in0(4'b1100), .in1(4'b1101), .in2(4'b1111), .in3({not_1_out[3], Instruction[8:6]}), .out(WA),
    .sel(WA_SELECT[1:0]));
  Multiplexer #(.select(2), .width(4)) multiplexer_3 (
    .in0({1'b0, Instruction[8:6]}), .in1({Instruction[9], Instruction[5:3]}), .in2(Instruction[9:6]),
    .in3(4'b0000), .out(RA2), .sel(RA2_SELECT));
  Sex_6_16 sex_6_16_1 (.A(Instruction[5:0]), .B(sex_6_16_1_b));
  Sex_4_16 sex_4_16_1 (.A({Instruction[5], Instruction[9], Instruction[4:3]}), .B(sex_4_16_1_b));
  Sex_6_16 sex_6_16_2 (.A({Instruction[5], Instruction[9:6], Instruction[4]}), .B(sex_6_16_2_b));
  Sex_10_16 sex_10_16_1 (.A({Instruction[5], Instruction[9:6], Instruction[4:0]}), .B(sex_10_16_1_b));
  Multiplexer #(.select(3), .width(16)) multiplexer_4 (
    .in0({16{1'b0}}), .in1(16'h1), .in2({16{1'b1}}), .in4(sex_6_16_1_b), .in5(sex_4_16_1_b),
    .in6(sex_6_16_2_b), .in7(sex_10_16_1_b), .out(CONST), .sel(CONST_SELECT));  // open: in3

  assign IRQ_CODE = Instruction[3:0];
  assign TIMER_DELAY = Instruction[3:0];

  // Notes on the sheet:
  //   contents of rom_1 (hex, n*v repeats v):
  //   16*1fffffffff 653f1ff9 668132db 1fa3813ef3 247ab03f 1f8a8d00d1 4e21a106 1f91b67233 1fef80e551
  //   3343e6d 1fcb819ee8 796e9bc2 1ffa041a92 3fd446d2 1fcc8d7aa6 1fee3f4150 1f8d8cf6e1 1f905a47f7 6b14c57a
  //   1f9c1333be 7100174 1fa235ba49 1fadc02232 760d41a3 1fdce1d850 1feba3bb2a 6b8263af 1fdb1eb9ca 718bb6d1
  //   1fe21b376d 1fc79efb68 24fbbdb2 313a4c29 1fd123e5dc 1fa59fb7e4 4157640c 1fb4c0e1d9 1fc62211b3
  //   45d3d343 4891ab41 4a6ad239 4ce13522 1ff43251b6 1f80413bea 52154ef6 1fa7e763ce 54b9b003 1fdb42fb56
  //   4f4b778e
endmodule

module Add1_16 (
  input  [15:0] A,
  output [15:0] S
);

  wire adder_1_cout, adder_2_cout, adder_3_cout;

  Adder #(.width(4)) adder_1 (.a(A[3:0]), .b(4'b0001), .out(S[3:0]), .cout(adder_1_cout));  // open: cin
  Adder #(.width(4)) adder_2 (.a(A[7:4]), .b(4'b0000), .out(S[7:4]), .cin(adder_1_cout), .cout(adder_2_cout));
  Adder #(.width(4)) adder_3 (.a(A[11:8]), .b(4'b0000), .out(S[11:8]), .cin(adder_2_cout), .cout(adder_3_cout));
  Adder #(.width(4)) adder_4 (.a(A[15:12]), .b(4'b0000), .out(S[15:12]), .cin(adder_3_cout));  // open: cout
endmodule

module Sex_10_16 (
  input  [9:0] A,
  output [15:0] B
);

  wire bitselector_1_out, buffer_1_out;

  buf buffer_1 (buffer_1_out, bitselector_1_out);
  BitSelector #(.width(10)) bitselector_1 (.in(A), .out(bitselector_1_out), .sel(4'b1001));
  buf buffer_2 (B[11], buffer_1_out);
  buf buffer_3 (B[13], buffer_1_out);
  buf buffer_4 (B[15], buffer_1_out);

  assign {B[14], B[12], B[10:0]} = {B[15], B[13], B[11], A};
endmodule

module Sex_6_16 (
  input  [5:0] A,
  output [15:0] B
);

  wire bitselector_1_out, buffer_1_out, buffer_3_out, buffer_7_out;

  BitSelector #(.width(6)) bitselector_1 (.in(A), .out(bitselector_1_out), .sel(3'b101));
  buf buffer_1 (buffer_1_out, bitselector_1_out);
  buf buffer_2 (B[7], buffer_3_out);
  buf buffer_3 (buffer_3_out, buffer_1_out);
  buf buffer_4 (B[9], buffer_3_out);
  buf buffer_5 (B[11], buffer_1_out);
  buf buffer_6 (B[13], buffer_7_out);
  buf buffer_7 (buffer_7_out, buffer_1_out);
  buf buffer_8 (B[15], buffer_7_out);

  assign {B[14], B[12], B[10], B[8], B[6:0]} = {B[15], B[13], B[11], B[9], B[7], A};
endmodule

module Sex_4_16 (
  input  [3:0] A,
  output [15:0] B
);

  wire bitselector_1_out, buffer_1_out, buffer_2_out, buffer_3_out, buffer_4_out;

  buf buffer_1 (buffer_1_out, bitselector_1_out);
  BitSelector #(.width(4)) bitselector_1 (.in(A), .out(bitselector_1_out), .sel(2'b11));
  buf buffer_2 (buffer_2_out, buffer_1_out);
  buf buffer_3 (buffer_3_out, buffer_1_out);
  buf buffer_4 (buffer_4_out, buffer_1_out);
  buf buffer_5 (B[5], buffer_2_out);
  buf buffer_6 (B[7], buffer_2_out);
  buf buffer_7 (B[9], buffer_3_out);
  buf buffer_8 (B[11], buffer_3_out);
  buf buffer_9 (B[13], buffer_4_out);
  buf buffer_10 (B[15], buffer_4_out);

  assign {B[14], B[12], B[10], B[8], B[6], B[4:0]} = {B[15], B[13], B[11], B[9], B[7], B[5], A};
endmodule

module Timer (
  input  CLK,
  input  [3:0] DELAY,
  input  SET,
  output TRIGGER
);

  wire counter_1_carry, or_1_out;
  wire [3:0] TimerDelay_q;
  wire [9:0] counter_1_q;

  Register #(.width(4)) TimerDelay (.D(DELAY), .en(SET), .clk(CLK), .Q(TimerDelay_q));  // open: clr
  Counter #(.max('h3ff), .ongoal("load"), .width(10)) counter_1 (
    .clr(1'b0), .load(1'b0), .up(1'b0), .count(1'b1), .clk(CLK), .D({TimerDelay_q, {6{1'b0}}}),
    .carry(counter_1_carry), .Q(counter_1_q));
  // NoConnect on counter_1_q
  or or_1 (or_1_out, TimerDelay_q[0], TimerDelay_q[1], TimerDelay_q[2], TimerDelay_q[3]);
  and and_1 (TRIGGER, counter_1_carry, or_1_out);
endmodule

module TickCounter (
  input  Reset,
  input  CLK,
  output [15:0] Ticks
);

  wire counter_1_carry;

  Counter #(.max('hffff), .width(16)) counter_1 (
    .clr(Reset), .load(1'b0), .up(1'b1), .count(1'b1), .clk(CLK), .D({16{1'b0}}), .carry(counter_1_carry),
    .Q(Ticks));
  // NoConnect on counter_1_carry
endmodule

module DLatch (
  input  D,
  input  EN,
  output Q
);

  wire nand_1_out, nand_2_out, nand_4_out, not_1_out;

  not not_1 (not_1_out, D);
  nand nand_1 (nand_1_out, D, EN);
  nand nand_2 (nand_2_out, EN, not_1_out);
  nand nand_3 (Q, nand_1_out, nand_4_out);
  nand nand_4 (nand_4_out, Q, nand_2_out);
endmodule
